# Fritzing sketch sketch (saved by Fritzing 0.9.3b)
breadboards: 1

parts:
  Composant1 = Adafruit Feather M0 Bluefruit LE [part_number="Adafruit #2995"]
  JP1 = Header 6 [package=1x06-smd]
  JP2 = Header 6 [package=1x06-smd]  # not connected
  J1 = JST-B3P-VH [part_number=JST-B3P-VH package=THT]

nets:
  N1: Composant1.A0, JP1.3
  N2: Composant1.GND, JP1.2, JP1.5, J1.pin3
  N3: Composant1.+3V3, JP1.1
  N4: Composant1.VBUS, JP1.6, J1.pin1
  N5: JP1.4, J1.pin2

custom parts:
  Adafruit Feather M0 Bluefruit LE: This is the Adafruit Feather M0 Bluefruit LE - our take on an 'all-in-one' Arduino-compatible + Bluetooth Low Energy with built in USB and battery charging. Its an Adafruit Feather M0 with a BTLE module, ready to rock! We have other boards in the Feather family, check'em out here. Bluetooth Low Energy is the hottest new low-power, 2.4GHz spectrum wireless protocol. In particular, its the only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
